// Logisim project 8bit_CPU.circ as structural Verilog: 3 circuits, main circuit main
module main (
  input  RESB,
  input  [15:0] ResetVectorLB,
  input  [15:0] ResetVectorHB,
  output [7:0] D0_7pins
);

  wire AC_DB, AC_SB, ACR, ACR_C, ADD_ADL, ADD_SB06, ADD_SB7, adder_1_cout, ADH_ABH, ADH_PCH, ADL_ABL,
       ADL_ADD, ADL_PCL, and_1_out, and_6_out, and_7_out, ANDS, AVR, AVR_V, B, bitselector_1_out, C, CL1,
       CL2, D, DAA, DB0_C, DB1_Z, DB2_I, DB3_D, DB6_V, DB7_N, DB_ADD, DBx_ADD, DBZ_Z, decoder_1_out0,
       decoder_1_out1, decoder_2_out1, decoder_2_out3, DL_ADH, DL_ADL, DL_DB, DSA, EORS, HC, I, I_ADDC, I_PC,
       I_V, IR5_C, IR5_D, IR5_I, N, not_5_out, O_ADD, O_ADH0, O_ADH17, O_ADL0, O_ADL1, O_ADL2, or_1_out,
       or_3_out, or_4_out, or_5_out, or_6_out, or_7_out, or_8_out, ORS, P_DB, PCH_ADH, PCH_DB, PCH_PCH,
       PCL_ADL, PCL_DB, PCL_PCL, pull_resistor_3_node, pull_resistor_6_node, RST, RST_q, RSTHB_ADB,
       RSTLB_ADB, RW, S_ADL, S_SB, SB_AC, SB_ADD, SB_ADH, SB_DB, SB_S, SB_X, SB_Y, SRS, SUMS, V, X_SB, Y_SB,
       Z;
  wire [1:0] priority_encoder_1_out, priority_encoder_2_out, priority_encoder_3_out, priority_encoder_4_out,
       priority_encoder_5_out;
  wire [3:0] counter_1_q;
  wire [5:5] P_q;
  wire [6:0] controlled_buffer_20_out, pull_resistor_7_node;
  wire [7:0] ABH_q, ABL_q, AC_q, ADD_q, adder_1_out, adder_2_out, AI_q, alu_1_alu_out, BI_q,
       bit_extender_2_out, controlled_buffer_2_out, controlled_buffer_3_out, controlled_buffer_6_out,
       controlled_buffer_9_out, controlled_buffer_14_out, controlled_buffer_22_out, controlled_buffer_27_out,
       DL_q, DOR_q, IR_q, multiplexer_4_out, not_4_out, PCH_q, PCHS_q, PCL_q, PCLS_q, PD_q,
       pull_resistor_4_node, ram_1_dout, rom_1_data, S_q, X_q, Y_q;
  wire [7:7] controlled_buffer_21_out;
  wire [15:0] ADB, and_8_out, and_9_out, bit_extender_3_out, bit_extender_4_out;
  wire [61:0] and_2_out, and_3_out, bit_extender_1_out, DecodePLA_out, not_3_out, ResetPLA_out;

  Clock clock_1 (.out(CL1));
  Register IR (.D(PD_q), .en(decoder_2_out1), .clk(CL1), .Q(IR_q), .clr(RST));
  not not_1 (RST, RESB);
  D_Flip_Flop u_RST (.D(RESB), .clk(RESB), .Q(RST_q), .reset(and_1_out));  // open: Qn, preset
  and and_1 (and_1_out, RST_q, decoder_2_out3);
  Decoder #(.enable("false"), .select(3)) decoder_1 (
    .out0(decoder_1_out0), .out1(decoder_1_out1), .sel(counter_1_q[2:0]));  // open: out2, out3, out4, out5, out6, out7
  not not_2 (CL2, CL1);
  or or_1 (or_1_out, RST, and_6_out);
  Counter #(.max('h7), .width(3)) counter_1 (
    .clr(or_1_out), .up(1'b1), .count(1'b1), .clk(CL2), .Q(counter_1_q[2:0]));  // open: load, D, carry
  Pull_Resistor pull_resistor_1 (.node(counter_1_q[3]));
  PLA #(.in_width(12), .out_width(62), .\table ("xxxxxxxxx000 00000000000000000000000000000000000000000000001000101001100000\nxxxxxxxxx001 00000000000000000000000000000000000000000000000001000010000000\n101000000010 00000000000000000000000000000000000000000000001000101001100000\n101000000011 01000000010000000000000100000001000010000000000001000010000001\n101000000100 00000000000000001000000011000000000000000000000000000000000000\n101001010010 00000000000000000000000000000000000000000000001000101001100000\n101001010011 00000000000000000000000000000000000000000000000001000011111010\n101001010100 01000000010000000010000100000001000010000000000000000000000001\n101001010101 00000000000000000000010011000000000000000000000000000000000000\n101010010010 00000000000000000000000000000000000000000000001000101001100000\n101010010011 01000000010000000010000100000001000010000000000001000010000001\n101010010100 00000000000000000000010011000000000000000000000000000000000000\n101011010010 00000000000000000000000000000000000000000000001000101001100000\n101011010011 00000000000000000000000100000000000010000000000001000010000001\n101011010100 00000000000000000000000000000001000000000000001000100001100000\n101011010101 00000000000000000000000000100000000000000000000000001001100100\n101011010110 01000000010000000010000100000001000010000000000001000010000001\n101011010111 00000000000000000000010011000000000000000000000000000000000000\n101110010010 00000000000000000000000000000000000000000000001000101001100000\n101110010011 00000000000100010000001000000001000010000000001001101011100001\n101110010100 00000000000000000000000100100001000010000000000001000011000001\n101110010101 00000000000001000000000011000000000000000000010000000000100000\n101110010110 00000000000000000000000101000001000010000000000000000000000001\n101110010111 01000000010000000000010011000000000000000000000000000000000000\n101111010010 00000000000000000000000000000000000000000000001000101001100000\n101111010011 00000000000000000000000100000000000010000000000001000010000001\n101111010100 00000000000000000000000000000001000000000000001000100001100000\n101111010101 00000000000000000000000000100000000000000000000000001001100100\n101111010110 01000000010000000010000100000001000010000000000001000010000001\n101111010111 00000000000000000000010011000000000000000000000000000000000000")) DecodePLA (
    .in({IR_q, counter_1_q}), .out(DecodePLA_out));
  PLA #(.in_width(3), .out_width(62), .\table ("000 00000000000000000000000100000001000001000000000000000000000000\n001 00000000000000000000000011000000000000010000000000000100000010\n010 00000000000000000000000000000000000000000000000010000000000100")) ResetPLA (
    .in(counter_1_q[2:0]), .out(ResetPLA_out));
  assign and_2_out = DecodePLA_out & not_3_out;  // AND_Gate and_2, 62 bits wide
  assign not_3_out = ~bit_extender_1_out;  // NOT_Gate not_3, 62 bits wide
  assign bit_extender_1_out = {{61{RST_q}}, RST_q};  // Bit_Extender bit_extender_1
  assign and_3_out = bit_extender_1_out & ResetPLA_out;  // AND_Gate and_3, 62 bits wide
  and and_4 (RSTLB_ADB, RST_q, decoder_1_out0);
  and and_5 (RSTHB_ADB, RST_q, decoder_1_out1);
  Register PD (.D(D0_7pins), .en(CL2), .clk(CL2), .Q(PD_q), .clr(RST));
  assign {RW, DB7_N, I_V, AVR_V, DB6_V, IR5_D, DB3_D, IR5_I, DB2_I, DBZ_Z, DB1_Z, ACR_C, IR5_C, DB0_C, P_DB, Y_SB, SB_Y, X_SB, SB_X, AC_SB, AC_DB, SB_AC, SB_ADD, O_ADD, ADD_SB7, ADD_SB06, ADD_ADL, SRS, ORS, EORS, ANDS, SUMS, DSA, DAA, I_ADDC, ADL_ADD, DB_ADD, DBx_ADD, S_SB, SB_S, S_ADL, O_ADL2, O_ADL1, O_ADL0, SB_DB, SB_ADH, PCH_ADH, PCH_DB, ADH_PCH, PCH_PCH, PCL_ADL, PCL_DB, I_PC, ADL_PCL, PCL_PCL, ADL_ABL, ADH_ABH, O_ADH17, O_ADH0, DL_ADH, DL_ADL, DL_DB} = and_2_out | and_3_out;  // OR_Gate or_2, 62 bits wide
  Decoder #(.enable("false"), .select(3)) decoder_2 (
    .out1(decoder_2_out1), .out3(decoder_2_out3), .sel(counter_1_q[2:0]));  // open: out0, out2, out4, out5, out6, out7
  RAM #(.addrWidth(16), .enables("line")) ram_1 (.addr(ADB), .we(RW), .clk(CL1), .din(D0_7pins), .dout(ram_1_dout));
  Register DOR (.D(controlled_buffer_2_out), .en(CL1), .clk(CL1), .Q(DOR_q), .clr(RST));
  assign D0_7pins = RW ? DOR_q : 8'bz;  // Controlled_Buffer controlled_buffer_1
  and and_6 (and_6_out, decoder_2_out3, RST_q);
  assign controlled_buffer_2_out = DL_DB ? DL_q : 8'bz;  // Controlled_Buffer controlled_buffer_2
  Pull_Resistor pull_resistor_2 (.node(controlled_buffer_2_out));
  BitSelector bitselector_1 (.in(IR_q), .out(bitselector_1_out), .sel(3'b101));
  and and_7 (and_7_out, ADB[15], ADB[14], ADB[13]);
  Multiplexer #(.width(8)) multiplexer_1 (.in0(ram_1_dout), .in1(rom_1_data), .out(D0_7pins), .sel(and_7_out));
  assign not_4_out = ~controlled_buffer_2_out;  // NOT_Gate not_4, 8 bits wide
  assign controlled_buffer_3_out = DBx_ADD ? not_4_out : 8'bz;  // Controlled_Buffer controlled_buffer_3
  ROM #(.addrWidth(13)) rom_1 (.addr(ADB[12:0]), .data(rom_1_data));
  assign controlled_buffer_2_out = PCL_DB ? PCL_q : 8'bz;  // Controlled_Buffer controlled_buffer_4
  assign controlled_buffer_3_out = DB_ADD ? controlled_buffer_2_out : 8'bz;  // Controlled_Buffer controlled_buffer_5
  or or_3 (or_3_out, C, I_ADDC);
  Register AI (.D(controlled_buffer_14_out), .en(or_6_out), .clk(CL1), .Q(AI_q), .clr(RST));
  Multiplexer #(.select(2)) multiplexer_2 (
    .in0(I), .in1(controlled_buffer_2_out[2]), .in2(bitselector_1_out), .out(multiplexer_4_out[2]),
    .sel(priority_encoder_1_out));  // open: in3
  Priority_Encoder #(.select(2)) priority_encoder_1 (
    .in0(1'b1), .in1(DB2_I), .in2(IR5_I), .in3(1'b0), .out(priority_encoder_1_out));
  Multiplexer multiplexer_3 (.in0(N), .in1(controlled_buffer_2_out[7]), .out(multiplexer_4_out[7]), .sel(DB7_N));
  or or_4 (or_4_out, ADL_PCL, PCL_PCL);
  assign controlled_buffer_6_out = PCL_PCL ? PCL_q : 8'bz;  // Controlled_Buffer controlled_buffer_6
  or or_5 (or_5_out, DBx_ADD, DB_ADD, ADL_ADD);
  Multiplexer #(.select(2)) multiplexer_4 (
    .in0(C), .in1(controlled_buffer_2_out[0]), .in2(bitselector_1_out), .in3(ACR),
    .out(multiplexer_4_out[0]), .sel(priority_encoder_2_out));
  Priority_Encoder #(.select(2)) priority_encoder_2 (
    .in0(1'b1), .in1(DB0_C), .in2(IR5_C), .in3(ACR_C), .out(priority_encoder_2_out));
  Multiplexer #(.select(2)) multiplexer_5 (
    .in0(Z), .in1(controlled_buffer_2_out[1]), .in2(not_5_out), .out(multiplexer_4_out[1]),
    .sel(priority_encoder_3_out));  // open: in3
  Priority_Encoder #(.select(2)) priority_encoder_3 (
    .in0(1'b1), .in1(DB1_Z), .in2(DBZ_Z), .in3(1'b0), .out(priority_encoder_3_out));
  Multiplexer #(.select(2)) multiplexer_6 (
    .in0(D), .in1(controlled_buffer_2_out[3]), .in2(bitselector_1_out), .out(multiplexer_4_out[3]),
    .sel(priority_encoder_4_out));  // open: in3
  Priority_Encoder #(.select(2)) priority_encoder_4 (
    .in0(1'b1), .in1(DB3_D), .in2(IR5_D), .in3(1'b0), .out(priority_encoder_4_out));
  Multiplexer #(.select(2)) multiplexer_7 (
    .in0(V), .in1(controlled_buffer_2_out[6]), .in2(AVR), .in3(1'b1), .out(multiplexer_4_out[6]),
    .sel(priority_encoder_5_out));
  Priority_Encoder #(.select(2)) priority_encoder_5 (
    .in0(1'b1), .in1(DB6_V), .in2(AVR_V), .in3(I_V), .out(priority_encoder_5_out));
  assign controlled_buffer_6_out = ADL_PCL ? controlled_buffer_9_out : 8'bz;  // Controlled_Buffer controlled_buffer_7
  Register PCLS (.D(controlled_buffer_6_out), .en(or_4_out), .clk(CL1), .Q(PCLS_q), .clr(RST));
  assign bit_extender_2_out = {{7{1'b0}}, I_PC};  // Bit_Extender bit_extender_2
  Register PCL (.D(adder_1_out), .en(CL2), .clk(CL2), .Q(PCL_q), .clr(RST));
  assign controlled_buffer_3_out = ADL_ADD ? controlled_buffer_9_out : 8'bz;  // Controlled_Buffer controlled_buffer_8
  Register BI (.D(controlled_buffer_3_out), .en(or_5_out), .clk(CL1), .Q(BI_q), .clr(RST));
  Register DL (.D(D0_7pins), .en(CL2), .clk(CL2), .Q(DL_q), .clr(RST));
  Adder adder_1 (.a(PCLS_q), .b(bit_extender_2_out), .out(adder_1_out), .cout(adder_1_cout));  // open: cin
  assign controlled_buffer_9_out[0] = O_ADL0 ? pull_resistor_3_node : 1'bz;  // Controlled_Buffer controlled_buffer_9
  assign controlled_buffer_9_out[1] = O_ADL1 ? pull_resistor_3_node : 1'bz;  // Controlled_Buffer controlled_buffer_10
  assign controlled_buffer_9_out[2] = O_ADL2 ? pull_resistor_3_node : 1'bz;  // Controlled_Buffer controlled_buffer_11
  Pull_Resistor pull_resistor_3 (.node(pull_resistor_3_node));
  ALU alu_1 (
    .CARRY_IN(or_3_out), .DAA(DAA), .BI(BI_q), .SUMS(SUMS), .ANDS(ANDS), .EORS(EORS), .ORS(ORS), .SRS(SRS),
    .AI(AI_q), .ALU_OUT(alu_1_alu_out), .HC(HC), .AVR(AVR), .ACR(ACR));
  assign controlled_buffer_9_out = DL_ADL ? DL_q : 8'bz;  // Controlled_Buffer controlled_buffer_12
  assign controlled_buffer_9_out = PCL_ADL ? PCL_q : 8'bz;  // Controlled_Buffer controlled_buffer_13
  Register ADD (.D(alu_1_alu_out), .en(CL2), .clk(CL2), .Q(ADD_q), .clr(RST));
  Pull_Resistor pull_resistor_4 (.node(pull_resistor_4_node));
  or or_6 (or_6_out, O_ADD, SB_ADD);
  assign controlled_buffer_14_out = O_ADD ? pull_resistor_4_node : 8'bz;  // Controlled_Buffer controlled_buffer_14
  Register P (
    .D({multiplexer_4_out[7:6], 2'b10, multiplexer_4_out[3:0]}), .en(SB_X), .clk(CL1),
    .Q({N, V, P_q[5], B, D, I, Z, C}), .clr(RST));
  // NoConnect on P_q[5]
  assign controlled_buffer_9_out = ADD_ADL ? ADD_q : 8'bz;  // Controlled_Buffer controlled_buffer_15
  assign controlled_buffer_14_out = SB_ADD ? {controlled_buffer_21_out[7], controlled_buffer_20_out} : 8'bz;  // Controlled_Buffer controlled_buffer_16
  assign controlled_buffer_2_out = P_DB ? {N, V, P_q[5], B, D, I, Z, C} : 8'bz;  // Controlled_Buffer controlled_buffer_17
  or or_7 (or_7_out, ADH_PCH, PCH_PCH);
  assign controlled_buffer_2_out = PCL_DB ? PCH_q : 8'bz;  // Controlled_Buffer controlled_buffer_18
  assign controlled_buffer_9_out = S_ADL ? S_q : 8'bz;  // Controlled_Buffer controlled_buffer_19
  assign controlled_buffer_20_out = ADD_SB06 ? ADD_q[6:0] : 7'bz;  // Controlled_Buffer controlled_buffer_20
  assign controlled_buffer_21_out[7] = ADD_SB7 ? ADD_q[7] : 1'bz;  // Controlled_Buffer controlled_buffer_21
  or or_8 (or_8_out, controlled_buffer_2_out[7], controlled_buffer_2_out[6], controlled_buffer_2_out[5], controlled_buffer_2_out[4], controlled_buffer_2_out[3], controlled_buffer_2_out[2], controlled_buffer_2_out[1], controlled_buffer_2_out[0]);
  not not_5 (not_5_out, or_8_out);
  assign controlled_buffer_22_out = ADH_PCH ? controlled_buffer_27_out : 8'bz;  // Controlled_Buffer controlled_buffer_22
  assign controlled_buffer_22_out = PCH_PCH ? PCH_q : 8'bz;  // Controlled_Buffer controlled_buffer_23
  Register AC (.D({controlled_buffer_21_out[7], controlled_buffer_20_out}), .en(SB_AC), .clk(CL1), .Q(AC_q), .clr(RST));
  assign controlled_buffer_2_out = AC_DB ? AC_q : 8'bz;  // Controlled_Buffer controlled_buffer_24
  Register PCHS (.D(controlled_buffer_22_out), .en(or_7_out), .clk(CL1), .Q(PCHS_q), .clr(RST));
  Register PCH (.D(adder_2_out), .en(CL2), .clk(CL2), .Q(PCH_q), .clr(RST));
  assign controlled_buffer_2_out = SB_DB ? {controlled_buffer_21_out[7], controlled_buffer_20_out} : 8'bz;  // Controlled_Buffer controlled_buffer_25
  Register S (.D({controlled_buffer_21_out[7], controlled_buffer_20_out}), .en(SB_S), .clk(CL1), .Q(S_q), .clr(RST));
  Pull_Resistor pull_resistor_5 (.node({controlled_buffer_21_out[7], controlled_buffer_20_out}));
  Adder adder_2 (.a(PCHS_q), .b({8{1'b0}}), .out(adder_2_out), .cin(adder_1_cout));  // open: cout
  assign {controlled_buffer_21_out[7], controlled_buffer_20_out} = AC_SB ? AC_q : 8'bz;  // Controlled_Buffer controlled_buffer_26
  assign controlled_buffer_27_out = DL_ADH ? DL_q : 8'bz;  // Controlled_Buffer controlled_buffer_27
  assign controlled_buffer_27_out = PCH_ADH ? PCH_q : 8'bz;  // Controlled_Buffer controlled_buffer_28
  assign controlled_buffer_27_out = SB_ADH ? {controlled_buffer_21_out[7], controlled_buffer_20_out} : 8'bz;  // Controlled_Buffer controlled_buffer_29
  assign {controlled_buffer_21_out[7], controlled_buffer_20_out} = S_SB ? S_q : 8'bz;  // Controlled_Buffer controlled_buffer_30
  Register ABH (.D(controlled_buffer_27_out), .en(ADH_ABH), .clk(CL1), .Q(ABH_q), .clr(RST));
  Register X (.D({controlled_buffer_21_out[7], controlled_buffer_20_out}), .en(SB_X), .clk(CL1), .Q(X_q), .clr(RST));
  assign {controlled_buffer_21_out[7], controlled_buffer_20_out} = X_SB ? X_q : 8'bz;  // Controlled_Buffer controlled_buffer_31
  Register Y (.D({controlled_buffer_21_out[7], controlled_buffer_20_out}), .en(SB_Y), .clk(CL1), .Q(Y_q), .clr(RST));
  assign {controlled_buffer_21_out[7], controlled_buffer_20_out} = Y_SB ? Y_q : 8'bz;  // Controlled_Buffer controlled_buffer_32
  assign controlled_buffer_27_out[7:1] = O_ADH17 ? pull_resistor_7_node : 7'bz;  // Controlled_Buffer controlled_buffer_33
  Register ABL (.D(controlled_buffer_9_out), .en(ADL_ABL), .clk(CL1), .Q(ABL_q), .clr(RST));
  Pull_Resistor pull_resistor_6 (.node(pull_resistor_6_node));
  assign controlled_buffer_27_out[0] = O_ADH0 ? pull_resistor_6_node : 1'bz;  // Controlled_Buffer controlled_buffer_34
  Pull_Resistor pull_resistor_7 (.node(pull_resistor_7_node));
  assign and_8_out = bit_extender_3_out & ResetVectorLB;  // AND_Gate and_8, 16 bits wide
  assign bit_extender_3_out = {{15{RSTLB_ADB}}, RSTLB_ADB};  // Bit_Extender bit_extender_3
  assign ADB = {ABH_q, ABL_q} | and_8_out | and_9_out;  // OR_Gate or_9, 16 bits wide
  assign bit_extender_4_out = {{15{RSTHB_ADB}}, RSTHB_ADB};  // Bit_Extender bit_extender_4
  assign and_9_out = bit_extender_4_out & ResetVectorHB;  // AND_Gate and_9, 16 bits wide

  // Notes on the sheet:
  //   ResetVectorLB: initial=0xfffc
  //   ResetVectorHB: initial=0xfffd
  //   contents of rom_1 (hex, n*v repeats v):
  //   a0 2 b9 2 8185*0 e0
endmodule

module BCD_ADD (
  input  [7:0] INPUT2,
  input  [7:0] INPUT1,
  input  CARRY_IN,
  output [3:0] D0,
  output [3:0] D1,
  output HC,
  output D2
);

  wire adder_1_cout, adder_3_cout, and_1_out, and_2_out, and_3_out, and_4_out;
  wire [3:0] adder_1_out, adder_3_out;
  wire [3:3] pull_resistor_1_node, pull_resistor_2_node;

  or or_1 (D2, adder_1_cout, and_1_out, and_2_out);
  and and_1 (and_1_out, adder_1_out[3], adder_1_out[2]);
  and and_2 (and_2_out, adder_1_out[3], adder_1_out[1]);
  Pull_Resistor pull_resistor_1 (.node(pull_resistor_1_node[3]));
  Adder #(.width(4)) adder_1 (.a(INPUT1[7:4]), .b(INPUT2[7:4]), .out(adder_1_out), .cin(HC), .cout(adder_1_cout));
  Adder #(.width(4)) adder_2 (
    .a(adder_1_out), .b({pull_resistor_1_node[3], {2{D2}}, pull_resistor_1_node[3]}), .out(D1));  // open: cin, cout
  or or_2 (HC, adder_3_cout, and_3_out, and_4_out);
  and and_3 (and_3_out, adder_3_out[3], adder_3_out[2]);
  and and_4 (and_4_out, adder_3_out[3], adder_3_out[1]);
  Pull_Resistor pull_resistor_2 (.node(pull_resistor_2_node[3]));
  Adder #(.width(4)) adder_3 (.a(INPUT1[3:0]), .b(INPUT2[3:0]), .out(adder_3_out), .cin(CARRY_IN), .cout(adder_3_cout));
  Adder #(.width(4)) adder_4 (
    .a(adder_3_out), .b({pull_resistor_2_node[3], {2{HC}}, pull_resistor_2_node[3]}), .out(D0));  // open: cin, cout
endmodule

module ALU (
  input  CARRY_IN,
  input  DAA,
  input  [7:0] BI,
  input  SUMS,
  input  ANDS,
  input  EORS,
  input  ORS,
  input  SRS,
  input  [7:0] AI,
  output [7:0] ALU_OUT,
  output HC,
  output AVR,
  output ACR
);

  wire adder_1_cout, and_1_out, and_4_out, and_6_out, and_7_out, and_9_out, bcd_add_1_d2, bitselector_1_out,
       bitselector_2_out, bitselector_3_out, bitselector_4_out, not_2_out, not_3_out, or_1_out, or_5_out,
       xor_2_out;
  wire [2:0] bit_extender_2_out;
  wire [7:0] adder_1_out, and_2_out, and_3_out, and_5_out, bcd_add_1_d0, bit_extender_1_out, not_1_out,
       or_2_out, or_3_out, shifter_1_out, xor_1_out;

  and and_1 (and_1_out, SUMS, adder_1_cout);
  assign bit_extender_1_out = {{7{DAA}}, DAA};  // Bit_Extender bit_extender_1
  Adder adder_1 (.a(BI), .b(AI), .out(adder_1_out), .cin(CARRY_IN), .cout(adder_1_cout));
  assign and_2_out = adder_1_out & not_1_out;  // AND_Gate and_2, 8 bits wide
  assign not_1_out = ~bit_extender_1_out;  // NOT_Gate not_1, 8 bits wide
  assign and_3_out = bit_extender_1_out & bcd_add_1_d0;  // AND_Gate and_3, 8 bits wide
  and and_4 (and_4_out, DAA, bcd_add_1_d2);
  BCD_ADD bcd_add_1 (
    .INPUT2(BI), .INPUT1(AI), .CARRY_IN(CARRY_IN), .D0(bcd_add_1_d0[3:0]), .D1(bcd_add_1_d0[7:4]), .HC(HC),
    .D2(bcd_add_1_d2));
  or or_1 (or_1_out, and_4_out, and_1_out);
  assign or_2_out = and_2_out | and_3_out;  // OR_Gate or_2, 8 bits wide
  assign bit_extender_2_out = {{2{1'b0}}, 1'b1};  // Bit_Extender bit_extender_2
  assign ALU_OUT = SUMS ? or_2_out : 8'bz;  // Controlled_Buffer controlled_buffer_1
  assign and_5_out = BI & AI;  // AND_Gate and_5, 8 bits wide
  assign ALU_OUT = ANDS ? and_5_out : 8'bz;  // Controlled_Buffer controlled_buffer_2
  assign xor_1_out = BI ^ AI;  // XOR_Gate xor_1, 8 bits wide
  assign ALU_OUT = EORS ? xor_1_out : 8'bz;  // Controlled_Buffer controlled_buffer_3
  assign or_3_out = BI | AI;  // OR_Gate or_3, 8 bits wide
  assign ALU_OUT = ORS ? or_3_out : 8'bz;  // Controlled_Buffer controlled_buffer_4
  assign ALU_OUT = SRS ? shifter_1_out : 8'bz;  // Controlled_Buffer controlled_buffer_5
  Shifter #(.shift("lr")) shifter_1 (.in(AI), .\dist (bit_extender_2_out), .out(shifter_1_out));
  BitSelector bitselector_1 (.in(AI), .out(bitselector_1_out), .sel(3'b000));
  and and_6 (and_6_out, bitselector_1_out, SRS);
  or or_4 (ACR, or_1_out, and_6_out);
  Pull_Resistor pull_resistor_1 (.node(ALU_OUT));
  BitSelector bitselector_2 (.in(ALU_OUT), .out(bitselector_2_out), .sel(3'b111));
  BitSelector bitselector_3 (.in(BI), .out(bitselector_3_out), .sel(3'b111));
  BitSelector bitselector_4 (.in(AI), .out(bitselector_4_out), .sel(3'b111));
  xor xor_2 (xor_2_out, bitselector_2_out, bitselector_3_out);
  and and_7 (and_7_out, bitselector_3_out, bitselector_4_out);
  not not_2 (not_2_out, bitselector_3_out);
  not not_3 (not_3_out, bitselector_4_out);
  and and_8 (AVR, xor_2_out, or_5_out);
  or or_5 (or_5_out, and_7_out, and_9_out);
  and and_9 (and_9_out, not_2_out, not_3_out);
  Pull_Resistor pull_resistor_2 ();  // open: node
endmodule
